# Fritzing sketch LaundryRecicleDevice (saved by Fritzing 1.0.1rc)

parts:
  U1 = Turbidity Sensor Probe [package=THT]
  U2 = DFRobot SEN0189 [package=THT]
  VALVE1 = Plastic Solenoid Valve
  VALVE2 = Plastic Solenoid Valve
  A1 = yf-s401 flow sensor [package=THT]
  A2 = yf-s401 flow sensor [package=THT]
  Componente1 = Dual MOSFETs PWM Module
  Componente2 = Dual MOSFETs PWM Module
  U3 = ESP32-38PinWide [part_number=ESP32-38PinWide]

nets:
  N1: U1.pin1, U2.P2_1
  N2: U1.pin2, U2.P2_2
  N3: U1.VCC, U2.P2_3
  N4: U2.P1_1, U3.GPIO32
  0V: U2.P1_2, A1.pin1, A2.pin1, Componente1.+VLOAD, Componente2.+VLOAD, U3.3.3
  GND: U2.P1_3, A1.pin2, A2.pin2, Componente1.-VLOAD, Componente2.-VLOAD, U3.GND
  N5: VALVE1.no_name_yet#1, Componente1.-VIN
  N6: VALVE1.no_name_yet#2, Componente1.+VIN
  N7: VALVE2.no_name_yet#1, Componente2.-VIN
  N8: VALVE2.no_name_yet#2, Componente2.+VIN
  N9: A1.pin3, U3.GPIO34
  N10: A2.pin3, U3.GPIO35
  N11: Componente1.TRIG/PWM, U3.GPIO25
  N12: Componente2.TRIG/PWM, U3.GPIO26

notes:
  Vcc: 12DC
  Pin: D25
  Vcc: 12DC
  Pin: D26
  Vcc: 3.3, Pin D32
  Sensor Turbidity
  Vcc: 3.3, Pin D35
  Sensor Flow
  Vcc: 3.3, Pin D34
  Sensor Flow

custom parts:
  Turbidity Sensor Probe: Turbidity sensor probe to the DFRobot measure module.
  DFRobot SEN0189: Turbidity sensor of DFRobot SEN0189
  yf-s401 flow sensor: Flow sensors sit in line with your water line, and uses a pinwheel sensor to measure how much liquid has moved through it.
  Dual MOSFETs PWM Module: Dual Mosfet PWM Module
  ESP32-38PinWide: Generic 38-Pin ESP32 with wide format (only access to one side of pins on a breadboard) based on Stephen Lilley's HiLetgo ESP-WROOM-32 ESP32 ESP-32S Development Board.
